// Logisim project alu.circ as structural Verilog: 10 circuits, main circuit main
module main (
  input  [31:0] X,
  input  [31:0] Y,
  input  [3:0] Switch,
  output Signed_Overflow,
  output Equal,
  output [31:0] Result
);

  wire add_overflow, sub_overflow;
  wire [31:0] add_result, addu_sum, and_output, demultiplexer_1_out5, demultiplexer_1_out6,
       demultiplexer_1_out7, demultiplexer_1_out8, demultiplexer_1_out9, demultiplexer_1_out10,
       demultiplexer_1_out14, demultiplexer_1_out15, demultiplexer_2_out0, demultiplexer_2_out1,
       demultiplexer_2_out2, demultiplexer_2_out5, demultiplexer_2_out6, demultiplexer_2_out7,
       demultiplexer_2_out8, demultiplexer_2_out9, demultiplexer_2_out10, demultiplexer_2_out14,
       demultiplexer_2_out15, or_output, shifter_1_out, shifter_2_out, shifter_3_out, slt_out, sltu_out,
       sub_result, subu_result;

  Demultiplexer #(.select(4), .width(32)) demultiplexer_1 (
    .out5(demultiplexer_1_out5), .out6(demultiplexer_1_out6), .out7(demultiplexer_1_out7),
    .out8(demultiplexer_1_out8), .out9(demultiplexer_1_out9), .out10(demultiplexer_1_out10),
    .out14(demultiplexer_1_out14), .out15(demultiplexer_1_out15), .in(X), .sel(Switch));  // open: out0, out1, out2, out3, out4, out11, out12, out13, en
  Demultiplexer #(.select(4), .width(32)) demultiplexer_2 (
    .out0(demultiplexer_2_out0), .out1(demultiplexer_2_out1), .out2(demultiplexer_2_out2),
    .out5(demultiplexer_2_out5), .out6(demultiplexer_2_out6), .out7(demultiplexer_2_out7),
    .out8(demultiplexer_2_out8), .out9(demultiplexer_2_out9), .out10(demultiplexer_2_out10),
    .out14(demultiplexer_2_out14), .out15(demultiplexer_2_out15), .in(Y), .sel(Switch));  // open: out3, out4, out11, out12, out13, en
  Equal equal_1 (.X(Y), .Y(X), .Output(Equal));
  \or  \or  (.X(demultiplexer_1_out10), .Y(demultiplexer_2_out10), .Output(or_output));
  add add (.X(demultiplexer_1_out5), .Y(demultiplexer_2_out5), .result(add_result), .overflow(add_overflow));
  Shifter #(.width(32)) shifter_1 (.in(demultiplexer_2_out0), .\dist (X[4:0]), .out(shifter_1_out));
  Shifter #(.width(32), .shift("lr")) shifter_2 (.in(demultiplexer_2_out1), .\dist (X[4:0]), .out(shifter_2_out));
  Shifter #(.width(32), .shift("ar")) shifter_3 (.in(demultiplexer_2_out2), .\dist (X[4:0]), .out(shifter_3_out));
  addu addu (.X(demultiplexer_1_out6), .Y(demultiplexer_2_out6), .sum(addu_sum));
  sub sub (.in_1(demultiplexer_1_out7), .in_2(demultiplexer_2_out7), .result(sub_result), .overflow(sub_overflow));
  subu subu (.in_1(demultiplexer_1_out8), .in_2(demultiplexer_2_out8), .result(subu_result));
  \and  \and  (.X(demultiplexer_1_out9), .Y(demultiplexer_2_out9), .Output(and_output));
  slt__signed_comparison slt (.X(demultiplexer_1_out14), .Y(demultiplexer_2_out14), .out(slt_out));
  sltu__unsigned_comparison sltu (.X(demultiplexer_1_out15), .Y(demultiplexer_2_out15), .out(sltu_out));
  Multiplexer #(.select(4), .width(32)) multiplexer_1 (
    .in0(shifter_1_out), .in1(shifter_2_out), .in2(shifter_3_out), .in5(add_result), .in6(addu_sum),
    .in7(sub_result), .in8(subu_result), .in9(and_output), .in10(or_output), .in14(slt_out), .in15(sltu_out),
    .out(Result), .sel(Switch));  // open: in3, in4, in11, in12, in13, en
  Multiplexer #(.select(4)) multiplexer_2 (
    .in0(1'b0), .in1(1'b0), .in2(1'b0), .in3(1'b0), .in4(1'b0), .in5(add_overflow), .in6(1'b0),
    .in7(sub_overflow), .in8(1'b0), .in9(1'b0), .in10(1'b0), .in11(1'b0), .in12(1'b0), .in13(1'b0),
    .in14(1'b0), .in15(1'b0), .out(Signed_Overflow), .sel(Switch));  // open: en

  // Other names for the same wires on the sheet: overflow = Signed_Overflow; S[3:0] = Switch

  // Notes on the sheet:
  //   INPUTS to your circuit
  //   DON'T CHANGE THE LOCATIONS OF THE INPUTS AND OUTPUTS!
  //   OUTPUTS from your circuit
endmodule

module Equal (
  input  [31:0] X,
  input  [31:0] Y,
  output Output
);

  Comparator #(.width(32), .mode("unsigned")) comparator_1 (.a(X), .b(Y), .eq(Output));  // open: gt, lt
endmodule

module add (
  input  [31:0] X,
  input  [31:0] Y,
  output [31:0] result,
  output overflow
);

  wire comparator_1_eq, comparator_2_eq, not_1_out;

  Adder #(.width(32)) adder_1 (.a(X), .b(Y), .out(result));  // open: cin, cout
  Comparator #(.width(1), .mode("unsigned")) comparator_1 (.a(X[31]), .b(Y[31]), .eq(comparator_1_eq));  // open: gt, lt
  Comparator #(.width(1), .mode("unsigned")) comparator_2 (
    .a(Y[31]), .b(result[31]), .eq(comparator_2_eq));  // open: gt, lt
  and and_1 (overflow, comparator_1_eq, not_1_out);
  not not_1 (not_1_out, comparator_2_eq);
endmodule

module addu (
  input  [31:0] X,
  input  [31:0] Y,
  output [31:0] sum
);

  Adder #(.width(32)) adder_1 (.a(X), .b(Y), .out(sum));  // open: cin, cout
endmodule

module sub (
  input  [31:0] in_1,
  input  [31:0] in_2,
  output [31:0] result,
  output overflow
);

  wire and_1_out, and_2_out, and_3_out, and_4_out, comparator_1_gt, comparator_1_lt, multiplexer_1_out,
       multiplexer_2_out, not_1_out, not_2_out, not_3_out;

  Comparator #(.width(1), .mode("unsigned")) comparator_1 (
    .a(in_1[31]), .b(in_2[31]), .gt(comparator_1_gt), .lt(comparator_1_lt));  // open: eq
  not not_1 (not_1_out, comparator_1_gt);
  Subtractor #(.width(32)) subtractor_1 (.a(in_1), .b(in_2), .out(result));  // open: bin, bout
  and and_1 (and_1_out, comparator_1_lt, not_2_out);
  not not_2 (not_2_out, comparator_1_lt);
  and and_2 (and_2_out, comparator_1_gt, not_1_out);
  Multiplexer multiplexer_1 (
    .in0(and_1_out), .in1(comparator_1_lt), .out(multiplexer_1_out), .sel(comparator_1_lt));  // open: en
  Multiplexer multiplexer_2 (
    .in0(and_2_out), .in1(comparator_1_gt), .out(multiplexer_2_out), .sel(comparator_1_gt));  // open: en
  not not_3 (not_3_out, result[31]);
  and and_3 (and_3_out, result[31], multiplexer_1_out);
  and and_4 (and_4_out, not_3_out, multiplexer_2_out);
  or or_1 (overflow, and_3_out, and_4_out);

  // Notes on the sheet:
  //   1; 0
  //   0; 1
endmodule

module subu (
  input  [31:0] in_1,
  input  [31:0] in_2,
  output [31:0] result
);

  Subtractor #(.width(32)) subtractor_1 (.a(in_1), .b(in_2), .out(result));  // open: bin, bout
endmodule

module \and  (
  input  [31:0] X,
  input  [31:0] Y,
  output [31:0] Output
);

  assign Output = X & Y;  // AND_Gate and_1, 32 bits wide
endmodule

module \or  (
  input  [31:0] X,
  input  [31:0] Y,
  output [31:0] Output
);

  assign Output = X | Y;  // OR_Gate or_1, 32 bits wide
endmodule

module slt__signed_comparison (
  input  [31:0] X,
  input  [31:0] Y,
  output [31:0] out
);

  Comparator #(.width(32)) comparator_1 (.a(X), .b(Y), .lt(out[0]));  // open: gt, eq

  assign out[31:1] = {31{1'b0}};
endmodule

module sltu__unsigned_comparison (
  input  [31:0] X,
  input  [31:0] Y,
  output [31:0] out
);

  Comparator #(.width(32), .mode("unsigned")) comparator_1 (.a(X), .b(Y), .lt(out[0]));  // open: gt, eq

  assign out[31:1] = {31{1'b0}};
endmodule
